# Fritzing sketch 8-bit Computer (saved by Fritzing 0.9.3b)
circuit board: 15.3416cm x 9.71329cm
breadboards: 1

parts:
  Atmega16_(CPU) = Atmega16 [package="DIP (Dual Inline) [THT]"]
  R1 = Resistor [tolerance=±5% resistance=220 package=THT]
  D5_LED = LED - 5mm [color="Red (633nm)" package="5 mm [THT]"]
  SRAM = UM61256FK-16 [chip_label=UM61256FK-16 package="DIP (Dual Inline) [THT]"]
  D0_LED = LED - 5mm [color="Red (633nm)" package="5 mm [THT]"]
  D4_LED = LED - 5mm [color="Red (633nm)" package="5 mm [THT]"]
  Pad1 = Pad [width=7.902222222222222 height=9.0311111111111106 connect=center]  # not connected
  D2_LED = LED - 5mm [color="Red (633nm)" package="5 mm [THT]"]
  D6_LED = LED - 5mm [color="Red (633nm)" package="5 mm [THT]"]
  D7_LED = LED - 5mm [color="Red (633nm)" package="5 mm [THT]"]
  C2 = Ceramic Capacitor [capacitance=22pF package="100 mil [THT, multilayer]"]
  XTAL1 = Crystal [frequency="16 Mhz" package=THT]
  C1 = Ceramic Capacitor [capacitance=22pF package="100 mil [THT, multilayer]"]
  D1_LED = LED - 5mm [color="Red (633nm)" package="5 mm [THT]"]
  CPU_stop = female pin header, 2 pins [form="♀ (female)"]
  D3_LED = LED - 5mm [color="Red (633nm)" package="5 mm [THT]"]
  Atmega328P_(video+sound_chip) = Atmega328P [package="DIP (Dual Inline) [THT]"]
  A3_LED = LED - 5mm [color="Red (633nm)" package="5 mm [THT]"]
  A0_LED = LED - 5mm [color="Red (633nm)" package="5 mm [THT]"]
  A1_LED = LED - 5mm [color="Red (633nm)" package="5 mm [THT]"]
  A14_LED = LED - 5mm [color="Red (633nm)" package="5 mm [THT]"]
  A2_LED = LED - 5mm [color="Red (633nm)" package="5 mm [THT]"]
  A13_LED = LED - 5mm [color="Red (633nm)" package="5 mm [THT]"]
  A12_LED = LED - 5mm [color="Red (633nm)" package="5 mm [THT]"]
  A11_LED = LED - 5mm [color="Red (633nm)" package="5 mm [THT]"]
  A10_LED = LED - 5mm [color="Red (633nm)" package="5 mm [THT]"]
  A9_LED = LED - 5mm [color="Red (633nm)" package="5 mm [THT]"]
  A8_LED = LED - 5mm [color="Red (633nm)" package="5 mm [THT]"]
  A7_LED = LED - 5mm [color="Red (633nm)" package="5 mm [THT]"]
  A6_LED = LED - 5mm [color="Red (633nm)" package="5 mm [THT]"]
  A5_LED = LED - 5mm [color="Red (633nm)" package="5 mm [THT]"]
  A4_LED = LED - 5mm [color="Red (633nm)" package="5 mm [THT]"]
  R3 = Resistor [tolerance=±5% resistance=330 package=THT]
  R4 = Resistor [tolerance=±5% resistance=330 package=THT]
  R5 = Resistor [tolerance=±5% resistance=330 package=THT]
  R7 = Resistor [tolerance=±5% resistance=330 package=THT]
  R8 = Resistor [tolerance=±5% resistance=330 package=THT]
  R9 = Resistor [tolerance=±5% resistance=330 package=THT]
  R10 = Resistor [tolerance=±5% resistance=330 package=THT]
  R11 = Resistor [tolerance=±5% resistance=330 package=THT]
  R12 = Resistor [tolerance=±5% resistance=330 package=THT]
  R13 = Resistor [tolerance=±5% resistance=330 package=THT]
  R14 = Resistor [tolerance=±5% resistance=330 package=THT]
  R15 = Resistor [tolerance=±5% resistance=330 package=THT]
  R16 = Resistor [tolerance=±5% resistance=330 package=THT]
  R17 = Resistor [tolerance=±5% resistance=330 package=THT]
  R18 = Resistor [tolerance=±5% resistance=330 package=THT]
  R19 = Resistor [tolerance=±5% resistance=330 package=THT]
  R20 = Resistor [tolerance=±5% resistance=330 package=THT]
  R21 = Resistor [tolerance=±5% resistance=330 package=THT]
  R22 = Resistor [tolerance=±5% resistance=330 package=THT]
  R23 = Resistor [tolerance=±5% resistance=330 package=THT]
  R24 = Resistor [tolerance=±5% resistance=330 package=THT]
  R25 = Resistor [tolerance=±5% resistance=330 package=THT]
  R26 = Resistor [tolerance=±5% resistance=330 package=THT]
  XTAL2 = Crystal [frequency="16 Mhz" package=THT]
  C4 = Ceramic Capacitor [capacitance=22pF package="100 mil [THT, multilayer]"]
  CPU_1-20 = female pin header, 20 pins [form="♀ (female)"]
  CPU_21-40 = female pin header, 20 pins [form="♀ (female)"]
  RAM_15-28 = female pin header, 14 pins [form="♀ (female)"]
  RAM_1-14 = female pin header, 14 pins [form="♀ (female)"]
  VIDEO15-28 = female pin header, 14 pins [form="♀ (female)"]
  VIDEO15-29 = female pin header, 14 pins [form="♀ (female)"]
  C3 = Ceramic Capacitor [capacitance=22pF package="100 mil [THT, multilayer]"]
  Q1 = NPN-Transistor [package="TO92 [THT]"]
  R27 = Resistor [tolerance=±5% resistance=4.7k package=THT]

nets:
  N1: Atmega16_(CPU).pin1, CPU_1-20.pin20
  N2: Atmega16_(CPU).pin2, CPU_1-20.pin19
  N3: Atmega16_(CPU).pin3, CPU_1-20.pin18
  N4: Atmega16_(CPU).pin4, CPU_1-20.pin17
  N5: Atmega16_(CPU).pin5, CPU_1-20.pin16
  N6: Atmega16_(CPU).pin6, CPU_1-20.pin15
  N7: Atmega16_(CPU).pin7, CPU_1-20.pin14
  N8: Atmega16_(CPU).pin8, CPU_1-20.pin13
  N9: Atmega16_(CPU).pin9, CPU_1-20.pin12
  5V: Atmega16_(CPU).pin10, Atmega16_(CPU).pin30, Atmega16_(CPU).pin32, R1.Pin_1, SRAM.pin28, Atmega328P_(video+sound_chip).pin7, CPU_21-40.pin9, CPU_21-40.pin11, RAM_15-28.pin1, VIDEO15-29.pin8, R27.Pin_1
  GND: Atmega16_(CPU).pin11, Atmega16_(CPU).pin31, SRAM.pin14, C2.0, C1.0, CPU_stop.pin2, Atmega328P_(video+sound_chip).pin8, Atmega328P_(video+sound_chip).pin22, R3.Pin_1, R4.Pin_1, R5.Pin_1, R7.Pin_1, R8.Pin_1, R9.Pin_1, R10.Pin_1, R11.Pin_1, R12.Pin_1, R13.Pin_1, R14.Pin_1, R15.Pin_1, R16.Pin_1, R17.Pin_1, R18.Pin_1, R19.Pin_1, R20.Pin_1, R21.Pin_1, R22.Pin_1, R23.Pin_1, R24.Pin_1, R25.Pin_1, R26.Pin_1, C4.0, CPU_1-20.pin10, CPU_21-40.pin10, RAM_1-14.pin1, VIDEO15-28.pin7, VIDEO15-29.pin7, C3.0
  N10: Atmega16_(CPU).pin12, C2.1, XTAL1.pin_0, CPU_1-20.pin9
  N11: Atmega16_(CPU).pin13, XTAL1.pin_1, C1.1, CPU_1-20.pin8
  N12: Atmega16_(CPU).pin14, R1.Pin_0, CPU_stop.pin1, CPU_1-20.pin7, CPU_1-20.pin11
  N13: Atmega16_(CPU).pin15, SRAM.pin1, A14_LED.anode, CPU_1-20.pin6, RAM_1-14.pin14
  N14: Atmega16_(CPU).pin16, SRAM.pin26, A13_LED.anode, CPU_1-20.pin5, RAM_15-28.pin3
  N15: Atmega16_(CPU).pin17, SRAM.pin2, A12_LED.anode, CPU_1-20.pin4, RAM_1-14.pin13
  N16: Atmega16_(CPU).pin18, SRAM.pin23, A11_LED.anode, CPU_1-20.pin3, RAM_15-28.pin6
  N17: Atmega16_(CPU).pin19, SRAM.pin21, A10_LED.anode, CPU_1-20.pin2, RAM_15-28.pin8
  N18: Atmega16_(CPU).pin20, SRAM.pin24, A9_LED.anode, CPU_1-20.pin1, RAM_15-28.pin5
  N19: Atmega16_(CPU).pin21, SRAM.pin25, A8_LED.anode, CPU_21-40.pin20, RAM_15-28.pin4
  N20: Atmega16_(CPU).pin22, SRAM.pin10, A0_LED.anode, CPU_21-40.pin19, RAM_1-14.pin5
  N21: Atmega16_(CPU).pin23, SRAM.pin9, A1_LED.anode, CPU_21-40.pin18, RAM_1-14.pin6
  N22: Atmega16_(CPU).pin24, SRAM.pin8, A2_LED.anode, CPU_21-40.pin17, RAM_1-14.pin7
  N23: Atmega16_(CPU).pin25, SRAM.pin7, A3_LED.anode, CPU_21-40.pin16, RAM_1-14.pin8
  N24: Atmega16_(CPU).pin26, SRAM.pin6, A4_LED.anode, CPU_21-40.pin15, RAM_1-14.pin9
  N25: Atmega16_(CPU).pin27, SRAM.pin5, A5_LED.anode, CPU_21-40.pin14, RAM_1-14.pin10
  N26: Atmega16_(CPU).pin28, SRAM.pin4, A6_LED.anode, CPU_21-40.pin13, RAM_1-14.pin11
  N27: Atmega16_(CPU).pin29, SRAM.pin3, A7_LED.anode, CPU_21-40.pin12, RAM_1-14.pin12
  N28: Atmega16_(CPU).pin33, SRAM.pin19, D7_LED.anode, Atmega328P_(video+sound_chip).pin13, CPU_21-40.pin8, RAM_15-28.pin10, VIDEO15-29.pin2
  N29: Atmega16_(CPU).pin34, SRAM.pin18, D6_LED.anode, Atmega328P_(video+sound_chip).pin12, CPU_21-40.pin7, RAM_15-28.pin11, VIDEO15-29.pin3
  N30: Atmega16_(CPU).pin35, D5_LED.anode, SRAM.pin17, Atmega328P_(video+sound_chip).pin11, CPU_21-40.pin6, RAM_15-28.pin12, VIDEO15-29.pin4
  N31: Atmega16_(CPU).pin36, SRAM.pin16, D4_LED.anode, Atmega328P_(video+sound_chip).pin6, CPU_21-40.pin5, RAM_15-28.pin13, VIDEO15-29.pin9
  N32: Atmega16_(CPU).pin37, SRAM.pin15, D3_LED.anode, Atmega328P_(video+sound_chip).pin5, CPU_21-40.pin4, RAM_15-28.pin14, VIDEO15-29.pin10
  N33: Atmega16_(CPU).pin38, SRAM.pin13, D2_LED.anode, Atmega328P_(video+sound_chip).pin4, CPU_21-40.pin3, RAM_1-14.pin2, VIDEO15-29.pin11
  N34: Atmega16_(CPU).pin39, SRAM.pin12, D1_LED.anode, Atmega328P_(video+sound_chip).pin3, CPU_21-40.pin2, RAM_1-14.pin3, VIDEO15-29.pin12
  N35: Atmega16_(CPU).pin40, SRAM.pin11, D0_LED.anode, Atmega328P_(video+sound_chip).pin2, CPU_21-40.pin1, RAM_1-14.pin4, VIDEO15-29.pin13
  N36: D5_LED.cathode, R12.Pin_0
  N37: SRAM.pin20, RAM_15-28.pin9, Q1.E, R27.Pin_0
  N38: SRAM.pin22, RAM_15-28.pin7
  N39: SRAM.pin27, RAM_15-28.pin2
  N40: D0_LED.cathode, R7.Pin_0
  N41: D4_LED.cathode, R11.Pin_0
  N42: D2_LED.cathode, R9.Pin_0
  N43: D6_LED.cathode, R13.Pin_0
  N44: D7_LED.cathode, R26.Pin_0
  N45: D1_LED.cathode, R8.Pin_0
  N46: D3_LED.cathode, R10.Pin_0
  N47: Atmega328P_(video+sound_chip).pin1, VIDEO15-29.pin14
  N48: Atmega328P_(video+sound_chip).pin9, XTAL2.pin_0, C4.1, VIDEO15-29.pin6
  N49: Atmega328P_(video+sound_chip).pin10, XTAL2.pin_1, VIDEO15-29.pin5, C3.1
  N50: Atmega328P_(video+sound_chip).pin14, VIDEO15-29.pin1
  N51: Atmega328P_(video+sound_chip).pin15, VIDEO15-28.pin14
  N52: Atmega328P_(video+sound_chip).pin16, VIDEO15-28.pin13
  N53: Atmega328P_(video+sound_chip).pin17, VIDEO15-28.pin12
  N54: Atmega328P_(video+sound_chip).pin18, VIDEO15-28.pin11
  N55: Atmega328P_(video+sound_chip).pin19, VIDEO15-28.pin10
  N56: Atmega328P_(video+sound_chip).pin20, VIDEO15-28.pin9
  N57: Atmega328P_(video+sound_chip).pin21, VIDEO15-28.pin8
  N58: Atmega328P_(video+sound_chip).pin23, VIDEO15-28.pin6
  N59: Atmega328P_(video+sound_chip).pin24, VIDEO15-28.pin5
  N60: Atmega328P_(video+sound_chip).pin25, VIDEO15-28.pin4
  N61: Atmega328P_(video+sound_chip).pin26, VIDEO15-28.pin3
  N62: Atmega328P_(video+sound_chip).pin27, VIDEO15-28.pin2
  N63: Atmega328P_(video+sound_chip).pin28, VIDEO15-28.pin1
  N64: A3_LED.cathode, R25.Pin_0
  N65: A0_LED.cathode, R3.Pin_0
  N66: A1_LED.cathode, R4.Pin_0
  N67: A14_LED.cathode, R14.Pin_0
  N68: A2_LED.cathode, R5.Pin_0
  N69: A13_LED.cathode, R15.Pin_0
  N70: A12_LED.cathode, R16.Pin_0
  N71: A11_LED.cathode, R17.Pin_0
  N72: A10_LED.cathode, R18.Pin_0
  N73: A9_LED.cathode, R19.Pin_0
  N74: A8_LED.cathode, R20.Pin_0
  N75: A7_LED.cathode, R21.Pin_0
  N76: A6_LED.cathode, R22.Pin_0
  N77: A5_LED.cathode, R23.Pin_0
  N78: A4_LED.cathode, R24.Pin_0

notes:
  8-bit computer, Alexandre Bergeron

custom parts:
  Atmega16: A DIP style package Atmega16. With 40 pins on a 600mil dual inline package (DIP) footprint.
  UM61256FK-16: A DIP style package 32K SRAM chip. With 28 pins on a 300mil dual inline package (DIP) footprint.
  Atmega328P: A DIP style package Atmega328P. With 28 pins on a 300mil dual inline package (DIP) footprint.

// code stored in the sketch: computerClock.ino
//common vars
int priority = 0;
bool canProceed = true;

//pin numbers
const int intPin = 2;
const int cpuPin = 6;
const int videoPin = 13;

void setup() {
  pinMode(intPin, INPUT);
  pinMode(cpuPin, OUTPUT);
  pinMode(videoPin, OUTPUT);
	//call function at startup
	procDone();
}

int procDone() {
	//reset pins
	digitalWrite(cpuPin, LOW);
	digitalWrite(videoPin, LOW);
	//give priority to next chip
	switch(priority) {
		case 0:
			digitalWrite(cpuPin, HIGH);
			break;
		case 1:
			digitalWrite(videoPin, HIGH);
			break;
	}
  priority++;
  if (priority==2) {
    priority = 0;
  }
}

void loop() {
  if (digitalRead(intPin)==HIGH) {
    if (canProceed==true) {
      canProceed=false;
      procDone();
      while(digitalRead(intPin)==HIGH) {
        delayMicroseconds(10);
      }
      canProceed=true;
    }
  }
}

// code stored in the sketch: computerCPU.ino
void setup() {
  // put your setup code here, to run once:

}

void loop() {
  // put your main code here, to run repeatedly:

}

// code stored in the sketch: computerVideo.ino
void setup() {
  // put your setup code here, to run once:

}

void loop() {
  // put your main code here, to run repeatedly:

}
